# Fritzing sketch ArenaSteuerungHBridge (saved by Fritzing 0.9.3b)
breadboards: 1

parts:
  Bauteil1 = Arduino Nano (Rev3.0)
  Button_ArenaMode = SWITCH-MOMENTARY-2 [package=tactile_switch_tall]
  Button_Obstacle = SWITCH-MOMENTARY-2 [package=tactile_switch_tall]
  Button_Timeout = SWITCH-MOMENTARY-2 [package=tactile_switch_tall]
  BeleuchtungArena = ws2812b [package="smd 2812b"]
  BeleuchtungPoller = ws2812b [package="smd 2812b"]
  Endstop_Oben = SWITCH-MOMENTARY-2 [package=tactile_switch_tall]
  Endstop_Unten = SWITCH-MOMENTARY-2 [package=tactile_switch_tall]
  V2 = DC Power [voltage=12V]
  H-Brücke = mystery part, 12 pins [chip_label=?]
  M1 = DC Motor
  Funkmodul = NRF24L01+ Breakout Board

nets:
  GND: Bauteil1.GND, Button_ArenaMode.2, Endstop_Oben.2, Endstop_Unten.2, Funkmodul.GND
  N1: Bauteil1.D2, Button_ArenaMode.1
  N2: Bauteil1.D3, Button_Timeout.1
  N3: Bauteil1.D4, Button_Obstacle.1
  N4: Bauteil1.D5, BeleuchtungArena.DIN
  N5: Bauteil1.D6, BeleuchtungPoller.DIN
  N6: Bauteil1.D7, Endstop_Oben.1
  N7: Bauteil1.D8, Endstop_Unten.1
  N8: Bauteil1.D9, H-Brücke.pin5
  N9: Bauteil1.D11/MOSI, Funkmodul.MOSI
  N10: Bauteil1.D12/MISO, Funkmodul.MISO
  N11: Bauteil1.A3, Funkmodul.CS
  N12: Bauteil1.A2, Funkmodul.CE
  N13: Bauteil1.A1, H-Brücke.pin6
  N14: Bauteil1.A0, H-Brücke.pin7
  3V3: Bauteil1.3V3, Funkmodul.VCC
  N15: Bauteil1.D13/SCK, Funkmodul.SCK
  N16: Button_Obstacle.2, Button_Timeout.2
  N17: V2.V+, H-Brücke.pin1
  N18: V2.V-, H-Brücke.pin2
  N19: H-Brücke.pin3, M1.pin_2
  N20: H-Brücke.pin4, M1.pin_1
