# Fritzing sketch ArenaSteuerungRelays (saved by Fritzing 0.9.3b)
breadboards: 1

parts:
  Bauteil1 = Arduino Nano (Rev3.0)
  Button_ArenaMode = SWITCH-MOMENTARY-2 [package=tactile_switch_tall]
  Button_Obstacle = SWITCH-MOMENTARY-2 [package=tactile_switch_tall]
  Button_Timeout = SWITCH-MOMENTARY-2 [package=tactile_switch_tall]
  BeleuchtungArena = ws2812b [package="smd 2812b"]
  BeleuchtungPoller = ws2812b [package="smd 2812b"]
  Endstop_Oben = SWITCH-MOMENTARY-2 [package=tactile_switch_tall]
  Endstop_Unten = SWITCH-MOMENTARY-2 [package=tactile_switch_tall]
  Poller_Relay_1 = Relay [part_number=FRS1B-S package=THT]
  V2 = DC Power [voltage=12V]
  M1 = DC Motor
  Poller_Relay_2 = Relay [part_number=FRS1B-S package=THT]

nets:
  N1: Bauteil1.GND, Button_ArenaMode.2, Endstop_Oben.2
  N2: Bauteil1.D2, Button_ArenaMode.1
  N3: Bauteil1.D3, Button_Timeout.1
  N4: Bauteil1.D4, Button_Obstacle.1
  N5: Bauteil1.D5, BeleuchtungArena.DIN
  N6: Bauteil1.D6, BeleuchtungPoller.DIN
  N7: Bauteil1.D7, Endstop_Oben.1
  N8: Bauteil1.D8, Endstop_Unten.1
  N9: Bauteil1.A1, Poller_Relay_2.COIL2
  N10: Bauteil1.A0, Poller_Relay_1.COIL2
  N11: Button_Obstacle.2, Button_Timeout.2
  N12: Endstop_Unten.2, Poller_Relay_1.COIL1, Poller_Relay_1.B, V2.V-, Poller_Relay_2.COIL1, Poller_Relay_2.B
  N13: Poller_Relay_1.A, V2.V+, Poller_Relay_2.A
  N14: Poller_Relay_1.C1, M1.pin_1
  N15: M1.pin_2, Poller_Relay_2.C1, Poller_Relay_2.C2
